# Fritzing sketch ESP32_Connections (saved by Fritzing 0.9.4)
breadboards: 2

parts:
  U1 = LCD-16X2 [package=lcd-16x2_noholes]
  LED1 = smd LED [color="Red (633nm)" package="0805 [SMD]"]
  Part1 = Passive Buzzer
  U3 = ESP32-38PinWide [part_number=ESP32-38PinWide]
  R1 = Resistor [tolerance=±5% resistance=10k package=THT]
  S1 = KY-026
  DHT1 = DHT11 Humitidy and Temperature Sensor
  Part2 = MQ-4
  ESP32_-_Back1 = ESP32 - CAM
  MCU1 = Raspberry Pi Zero
  GY-NEO6MV3 = SUP500F [package=sup500f]

nets:
  GND: U1.VSS, U1.R_W, U1.K, U3.GND, R1.Pin_0, GY-NEO6MV3.GND
  VDD: U1.VDD, U1.A, Part1.NC, S1.pin3, DHT1.VDD, Part2.VCC, GY-NEO6MV3.VCC
  N1: U1.VO, R1.Pin_1
  N2: U1.RS, U3.GPIO19
  N3: U1.E, U3.GPIO23
  N4: U1.DB4, U3.GPIO18
  N5: U1.DB5, U3.GPIO17, GY-NEO6MV3.TX-O
  N6: U1.DB6, U3.GPIO16, GY-NEO6MV3.RX-I
  N7: U1.DB7, U3.GPIO15
  GND_2: LED1.cathode, S1.pin2, DHT1.GND, Part2.GND
  N8: Part1.S, U3.GPIO21
  N9: U3.GPIO13, Part2.DO
  N10: U3.GPIO9, DHT1.DATA
  N11: ESP32_-_Back1.GND, MCU1.pin_34, MCU1.pin_39
  N12: ESP32_-_Back1.5V, MCU1.pin_2, MCU1.pin_4

custom parts:
  ESP32-38PinWide: Generic 38-Pin ESP32 with wide format (only access to one side of pins on a breadboard) based on Stephen Lilley's HiLetgo ESP-WROOM-32 ESP32 ESP-32S Development Board.
  KY-026: ky-026 flame sensor module
  DHT11 Humitidy and Temperature Sensor: DHT11 Humidity and Temperature Sensor
  ESP32 - CAM: The ESP32-CAM has a very competitive small-size camera module that can operate independently as a minimum system with a footprint of only 27*40.5*4.5mm and a deep sleep current of up to 6mA.

// code stored in the sketch: Untitled.ino

